# Fritzing sketch TB6612HBridgeNano (saved by Fritzing 0.9.3b)
breadboards: 1

parts:
  Part1 = Motor Driver 1A Dual TB6612FNG  # not connected
  M1 = DC Motor  # not connected
  R1 = Resistor [tolerance=±5% resistance=10k package="1206 [SMD]"]
  Part3 = Arduino Nano (Rev3.0)
  C2 = Electrolytic Capacitor [capacitance=100µF package="1010 [SMD, electrolytic]"]
  JACK2 = 2.1mm Barrel Jack with Terminal Block
  S2 = Toggle Switch [package=THT]
  R2 = Resistor [tolerance=±5% resistance=10k package=THT]

nets:
  N1: R1.Pin_1, Part3.3V3, C2.-, S2.COM
  N2: Part3.GND, C2.+, JACK2.NEG, R2.Pin_1
  N3: Part3.D2, S2.L2, R2.Pin_0
