# Fritzing sketch TB6612HBridgeUno (saved by Fritzing 0.9.9b)
breadboards: 1

parts:
  Part1 = Motor Driver 1A Dual TB6612FNG  # not connected
  M1 = DC Motor  # not connected
  R1 = Resistor [tolerance=±5% resistance=10k package="1206 [SMD]"]
  C2 = Electrolytic Capacitor [capacitance=100µF voltage=35V package="1010 [SMD, electrolytic]"]
  R2 = Resistor [tolerance=±5% resistance=10k power=0.25 package=THT]
  S2 = Pushbutton [package="[THT]"]
  Arduino2 = Arduino Uno (Rev3)

nets:
  N1: R1.Pin_1, C2.-, S2.Pin_3, S2.Pin_4, Arduino2.5V
  N2: C2.+, R2.Pin_1, Arduino2.GND
  N3: R2.Pin_0, S2.Pin_1, S2.Pin_2, Arduino2.D2
