# Fritzing sketch I2S_amp_circuit_MAX98357_nano_simple (saved by Fritzing 0.9.8b)
breadboards: 1

parts:
  SparkFun_I2S_Audio_Breakout2 = SparkFun_I2S_Audio_Breakout
  Part3 = Arduino Nano (Rev3.0)  # not connected
  Breakout_Board1 = Level Shifting uSD Breakout [package="DIP (Dual Inline) [THT]"]  # not connected
  TRS1 = Audio Jack (TRS) 3.5mm [package="4Ucon 08780 [THT]"]

nets:
  N1: SparkFun_I2S_Audio_Breakout2.OUT+, TRS1.Ring, TRS1.Tip
  N2: SparkFun_I2S_Audio_Breakout2.OUT-, TRS1.Sleeve

custom parts:
  SparkFun_I2S_Audio_Breakout: The SparkFun I2S Audio Breakout board uses the MAX98357A digital to analog converter (DAC), which converts I2S (not be confused with I2C) audio to an analog signal to drive speakers. The I2S Audio Breakout converts the digital audio signals using the I2S standard to an analog signal and amplifies the signal using a class D amplifier which can deliver up to 3.2W of power into a 4Ω load. The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
  Level Shifting uSD Breakout: Breakout board for the TI TXB0104 bi-directional level shifter IC. VccA should be lower than VccB. VccA can range from 1.2V to 3.6V, and VCCB can range from 1.65V to 5.5V.
