# Fritzing sketch TB6612HBridgeStepperUno (saved by Fritzing 0.9.9b)
breadboards: 1

parts:
  Arduino1 = Arduino Uno (Rev3)
  MOTOR2 = Adafruit Gear-Reduced Stepper Motor (small)  # not connected
  C1 = Capacitor Polarized [package=cpol-radial-10uf-25v]
  Part3 = Motor Driver 1A Dual TB6612FNG  # not connected
  R2 = Resistor [tolerance=±5% resistance=10k package="2010 [SMD]"]

nets:
  GND: Arduino1.GND, C1.-
  5V: Arduino1.5V, C1.+, R2.Pin_1

notes:
  Flip motor vertically after exporting to SVG

custom parts:
  Adafruit Gear-Reduced Stepper Motor (small): Adafruit gear-reduction stepper motor (small)
