# Fritzing sketch LabServoNano (saved by Fritzing 0.9.3b)
breadboards: 1

parts:
  R2 = Basic Force Sensing Resistor (FSR) [package=THT]
  R1 = Resistor [tolerance=±5% resistance=10k package=THT]
  Part1 = Arduino Nano (Rev3.0) (ICSP)
  J1 = Basic Servo

nets:
  3V3: R2.pin_0, Part1.3V3, J1.vcc
  N1: R2.pin_1, R1.Pin_1, Part1.AREF
  GND: R1.Pin_0, Part1.GND, J1.gnd
  N2: Part1.D3, J1.pulse
