# Fritzing sketch LabToneSimple (saved by Fritzing 0.9.3b)
breadboards: 1

parts:
  Arduino1 = Arduino Uno (Rev3)
  R3 = Resistor [tolerance=±5% resistance=100 package=THT]
  SPKR1 = Loudspeaker
  J1 = Basic Force Sensing Resistor (FSR) [package=THT]
  J2 = Basic Force Sensing Resistor (FSR) [package=THT]

nets:
  N1: Arduino1.A0, J1.pin_1, J2.pin_0
  N2: Arduino1.D8, SPKR1.pin2
  N3: Arduino1.5V, J1.pin_0
  GND: Arduino1.GND, R3.Pin_0, J2.pin_1
  N4: R3.Pin_1, SPKR1.pin1
