# Fritzing sketch UnipolarStepperLab (saved by Fritzing 0.8.0b)
breadboards: 1

parts:
  Arduino = Arduino Uno (Rev3)
  H-Bridge = L293D [package=THT]
  Unipolar_Stepper = Adafruit Gear-Reduced Stepper Motor (small)
  12V_Power_supply = 2.1mm Barrel Jack with Terminal Block

nets:
  N1: Arduino.GND, H-Bridge.0V, 12V_Power_supply.NEG
  N2: Arduino.D8, H-Bridge.In_1
  N3: Arduino.D9_PWM, H-Bridge.In_2
  N4: Arduino.D10_PWM/SS, H-Bridge.In_3
  N5: Arduino.D11_PWM/MOSI, H-Bridge.In_4
  N6: Arduino.5V, H-Bridge.Enable_1, H-Bridge.Enable_2, H-Bridge.+V
  N7: H-Bridge.Out_1_(_Controlled_by_Enable_1_), Unipolar_Stepper.PINK
  N8: H-Bridge.Out_2_(_Controlled_by_Enable_1_), Unipolar_Stepper.ORANGE
  N9: H-Bridge.+Vmotor, 12V_Power_supply.POS
  N10: H-Bridge.Out_3_(_Controlled_by_Enable_2_), Unipolar_Stepper.YELLOW
  N11: H-Bridge.Out_4_(_Controlled_by_Enable_2_), Unipolar_Stepper.BLUE

custom parts:
  Adafruit Gear-Reduced Stepper Motor (small): Adafruit gear-reduction stepper motor (small)
